# Fritzing sketch Schematics (saved by Fritzing 0.9.3b)
breadboards: 2

parts:
  L1 = Solenoid  # not connected
  Part1 = Arduino Mega 2560 (Rev3)
  LCD1 = LCD screen
  Part2 = Soil Moisture Sensor
  U1 = POT [package=pot_mammoth]
  DS1 = DS18B20 1-Wire Temperature Sensor [part_number=DS18B20]

nets:
  N1: Part1.A0, Part2.SIG
  N2: Part1.A1, DS1.DQ
  VDD: Part1.5V, LCD1.VDD, LCD1.LED+, Part2.VCC, DS1.VDD
  GND: Part1.GND, LCD1.LED-, Part2.GND, DS1.GND
  N3: Part1.D22, LCD1.RS
  N4: Part1.D24, LCD1.E
  N5: Part1.D26, LCD1.DB4
  N6: Part1.D28, LCD1.DB5
  N7: Part1.D30, LCD1.DB6
  N8: Part1.D32, LCD1.DB7
  N9: LCD1.VSS, U1.S
  N10: LCD1.V0, U1.A
